// Logisim project cpu.circ as structural Verilog: 1 circuit, main circuit main
module main (
  input  [31:0] INSTRUCTION,
  input  CLOCK,
  output [31:0] FETCH_ADDRESS,
  output [31:0] ra,
  output [31:0] sp,
  output [31:0] t0,
  output [31:0] t1,
  output [31:0] t2,
  output [31:0] s0,
  output [31:0] s1,
  output [31:0] a0
);

  wire DMEM_p1, DMEM_p4, DMEM_p7, DMEM_p10, DMEM_p13, RegFile_p1, RegFile_p3;
  wire [31:0] adder_1_out, PROGRAM_COUNTER;

  Adder #(.width(32)) adder_1 (.a(PROGRAM_COUNTER), .b(32'h4), .out(adder_1_out));  // open: cin, cout
  Register #(.width(32)) PC (.D(adder_1_out), .clk(CLOCK), .Q(PROGRAM_COUNTER));  // open: en, clr
  Shifter #(.width(32), .shift("lr")) shifter_1 (.in(PROGRAM_COUNTER), .\dist (5'b00010), .out(FETCH_ADDRESS));
  // regfile_main RegFile: pin names not known; wires that end beside it: RegFile_p1, ra, RegFile_p3
  // alu Arithmetic_Logic_Unit: pin names not known
  // mem_main DMEM: pin names not known; wires that end beside it: DMEM_p1, DMEM_p1, t1, DMEM_p4, DMEM_p4, t2, DMEM_p7, DMEM_p7, s0, DMEM_p10, DMEM_p10, s1, DMEM_p13, DMEM_p13, a0, RegFile_p1

  // Other names for the same wires on the sheet: clk = CLOCK

  // Notes on the sheet:
  //   Output
  //   Inputs/Outputs from run.circ. DO NOT MOVE THESE.
  //   Inputs
  //   It is OK to move the PC, RegFile, ALU, and MEM to wherever is most convenient for you when constructing your CPU, and to delete this text
  //   Inputs/Outputs from run.circ. DO NOT MOVE THESE.
endmodule
